# Fritzing sketch SmartFarm_with_DHT11_LCD (saved by Fritzing 0.9.9b)
breadboards: 1

parts:
  U1 = LCD-16X2 [package=lcd-16x2_nosilk]
  S1 = Pushbutton [package="[THT]"]
  S2 = Pushbutton [package="[THT]"]
  S3 = Pushbutton [package="[THT]"]
  부품1 = Arduino Uno (Rev3)
  R1 = Resistor [tolerance=±5% power=0.25 resistance=220 package=THT]
  J1 = Piezo Speaker
  R2 = Resistor [tolerance=±5% power=0.25 resistance=220 package=THT]
  R3 = Resistor [tolerance=±5% power=0.25 resistance=220 package=THT]
  DHT1 = DHT11 Humitidy and Temperature Sensor

nets:
  N1: U1.RS, U1.R_W, U1.E, U1.DB0, U1.DB1
  N2: U1.DB4, U1.DB6, R1.Pin_1, R2.Pin_1, R3.Pin_1, DHT1.VDD
  N3: U1.DB5, U1.DB7, S1.Pin_1, S1.Pin_2, S2.Pin_1, S2.Pin_2, S3.Pin_1, S3.Pin_2, DHT1.GND
  N4: U1.A, 부품1.A4/SDA
  N5: U1.K, 부품1.A5/SCL
  N6: S1.Pin_3, S1.Pin_4, 부품1.D5_PWM, R1.Pin_0
  N7: S2.Pin_3, S2.Pin_4, 부품1.D4, R2.Pin_0
  N8: S3.Pin_3, S3.Pin_4, 부품1.D2, R3.Pin_0
  N9: 부품1.D10_PWM/SS, J1.pin2
  N10: 부품1.D6_PWM, DHT1.DATA

custom parts:
  DHT11 Humitidy and Temperature Sensor: DHT11 Humidity and Temperature Sensor
